# Fritzing sketch Schematics (saved by Fritzing 0.9.3b)
breadboards: 1

parts:
  Part1 = Arduino Uno (Rev3)
  Raspberry_Pi_1 = Raspberry Pi 3 [part_number=RPI-3-V1.2]  # not connected
  LCD1 = LCD screen
  U1 = JOYSTICK-PSP1000 [package=joystick-psp1000]
  M1 = Stepper Motor - Bipolar
  M2 = Stepper Motor - Bipolar
  Pololu_A1 = Pololu A4988 [package=SO16]
  Pololu_A2 = Pololu A4988 [package=SO16]
  S1 = Pushbutton [package="[SMD]"]
  R1 = Resistor [tolerance=±5% resistance=220 package=THT]
  R2 = Resistor [tolerance=±5% resistance=220 package=THT]

nets:
  N1: Part1.A0, U1.X
  N2: Part1.A1, U1.Y
  N3: Part1.D8, Pololu_A1.DIR
  N4: Part1.D9_PWM, Pololu_A1.STEP
  N5: Part1.D10_PWM/SS, S1.Pin_1, S1.Pin_2, R1.Pin_1
  N6: Part1.D11_PWM/MOSI, LCD1.E
  N7: Part1.D12/MISO, LCD1.RS
  N8: Part1.D2, LCD1.DB7
  N9: Part1.D3_PWM, LCD1.DB6
  N10: Part1.D4, LCD1.DB5
  N11: Part1.D5_PWM, LCD1.DB4
  N12: Part1.D6_PWM, Pololu_A2.DIR
  N13: Part1.D7, Pololu_A2.STEP
  5V: Part1.5V, LCD1.VDD, LCD1.LED+, U1.VCC, S1.Pin_3, S1.Pin_4
  GND: Part1.GND, LCD1.VSS, LCD1.LED-, U1.GND, R1.Pin_0, R2.Pin_0
  N14: LCD1.V0, R2.Pin_1
  N15: M1.A, Pololu_A1.2B
  N16: M1.C, Pololu_A1.2A
  N17: M1.B, Pololu_A1.1A
  N18: M1.D, Pololu_A1.1B
  N19: M2.A, Pololu_A2.2B
  N20: M2.C, Pololu_A2.2A
  N21: M2.B, Pololu_A2.1A
  N22: M2.D, Pololu_A2.1B
